# Fritzing sketch sim800l-arduino (saved by Fritzing 0.9.3b)
breadboards: 1

parts:
  SIM800L_BO1 = SIM800L BO
  R1 = Resistor [tolerance=±5% resistance=1k package="0805 [SMD]"]
  Arduino_Uno = Arduino Uno (Rev3)
  BD139 = TRANSISTOR_NPN [package=to-92-ammo]

nets:
  N1: SIM800L_BO1.PIN3, BD139.C
  N2: SIM800L_BO1.pin_4, Arduino_Uno.D11_PWM/MOSI
  N3: SIM800L_BO1.pin_5, Arduino_Uno.D10_PWM/SS
  N4: SIM800L_BO1.pin_6, Arduino_Uno.GND, BD139.E
  N5: R1.Pin_0, BD139.B
  N6: R1.Pin_1, Arduino_Uno.D2
